# Fritzing sketch digispark-touchless (saved by Fritzing 0.9.4)
breadboards: 1

parts:
  Digispark1 = Digispark
  R1 = Resistor [tolerance=±5% resistance=10k package=THT]
  J1 = Infrared Proximity Sensor
  LED1 = LED - 5mm [color="Red (633nm)" package="5 mm [THT]"]

nets:
  VCC: Digispark1.VCC, J1.Vcc
  GND: Digispark1.GND, R1.Pin_1, J1.GND
  N1: Digispark1.P1, LED1.anode
  N2: Digispark1.P2, J1.Vout
  N3: R1.Pin_0, LED1.cathode

custom parts:
  Digispark: The Digispark is an Attiny85 based microcontroller development board similar to the Arduino line, only cheaper, smaller, and a bit less powerful. With a whole host of shields to extend its functionality and the ability to use the familiar Arduino IDE the Digispark is a great way to jump into electronics, or perfect for when an Arduino is too big or too much.
